// Logisim project infinityflipflop_SRND.circ as structural Verilog: 1 circuit, main circuit main
module main (
  input  in_1
);

  wire button_1_out, clock_1_out, d_ff_1_q, d_ff_1_qn, s_r_ff_1_q, s_r_ff_1_qn;

  LED led_1 (.in(d_ff_1_q));
  Clock clock_1 (.out(clock_1_out));
  S_R_Flip_Flop s_r_ff_1 (
    .S(s_r_ff_1_qn), .R(in_1), .clk(clock_1_out), .Q(s_r_ff_1_q), .reset(button_1_out), .Qn(s_r_ff_1_qn));  // open: preset
  Button button_1 (.out(button_1_out));
  D_Flip_Flop d_ff_1 (
    .D(d_ff_1_qn), .clk(s_r_ff_1_q), .Q(d_ff_1_q), .Qn(d_ff_1_qn), .reset(button_1_out));  // open: preset
endmodule
